# Fritzing sketch phoenicksboardv3 (saved by Fritzing 0.9.3b)
circuit board: 5.5cm x 5.7cm

parts:
  Raspberry_Pi_3 = Raspberry Pi 3 [part_number=RPI-3-V1.2]
  J1 = Power Jack [package=power_jack_pth]
  JP1 = Header 6 [package=molex-1x6-ra]
  U1 = M10X2 [package=2x10_lock_special]

nets:
  N1: Raspberry_Pi_3.GPIO4, U1.3
  N2: Raspberry_Pi_3.GPIO17, U1.5
  N3: Raspberry_Pi_3.GPIO27, U1.6
  N4: Raspberry_Pi_3.GPIO22, U1.7
  N5: Raspberry_Pi_3.GPIO6, JP1.6
  N6: Raspberry_Pi_3.GPIO13, JP1.5
  N7: Raspberry_Pi_3.GPIO19, JP1.2
  N8: Raspberry_Pi_3.GPIO26, JP1.1
  GND: Raspberry_Pi_3.GND, J1.GND, JP1.3, U1.1, U1.4, U1.10, U1.11
  N9: Raspberry_Pi_3.GPIO24, U1.9
  N10: Raspberry_Pi_3.GPIO23, U1.8
  N11: Raspberry_Pi_3.5V, U1.2, U1.12
  N12: J1.PWR, JP1.4

notes:
  GND
  VCC
  Golden Phoenicks™
  L1
  L2
  M1
  M2
  POWER
  Dunce
  LCD
  VERSION THREE
